// Logisim project logic_gates.circ as structural Verilog: 2 circuits, main circuit main
module main (
  input  A,
  input  A_2,
  input  A_3,
  input  A_4,
  input  A_5,
  input  A_6,
  input  A_7,
  input  A_8,
  input  B,
  input  B_2,
  input  B_3,
  input  B_4,
  input  B_5,
  input  B_6,
  input  in_15,
  input  in_16,
  input  in_17,
  input  in_18,
  input  in_19,
  input  in_20,
  input  in_21,
  input  in_22,
  input  in_23,
  input  in_24,
  input  in_25,
  input  in_26,
  output out_27,
  output out_28,
  output out_29,
  output out_30,
  output out_31,
  output out_32,
  output out_33,
  output out_34,
  output out_35,
  output out_36,
  output out_37,
  output out_38,
  output out_39,
  output out_40,
  output out_41,
  output out_42,
  output out_43,
  output out_44,
  output out_45,
  output out_46,
  output out_47,
  output out_48,
  output out_49,
  output out_50,
  output out_51
);

  wire and_2_out, and_4_out, nand_2_out, nand_3_out, nand_4_out, nand_5_out, nand_7_out, nand_8_out,
       nand_9_out, nand_10_out, nor_2_out, nor_3_out, nor_4_out, nor_5_out, nor_7_out, nor_8_out, nor_9_out,
       nor_10_out, or_2_out, or_3_out, pull_resistor_4_node, pull_resistor_8_node, pull_resistor_9_node,
       pull_resistor_11_node, pull_resistor_14_node, pull_resistor_15_node, pull_resistor_17_node,
       pull_resistor_18_node, pull_resistor_20_node, trnsstr_7_out_3, trnsstr_14_out_3, trnsstr_15_out_3,
       trnsstr_22_out_3;

  buf buffer_1 (out_28, A_5);
  trnsstr trnsstr_1 (.in_1(A_5), .in_2(1'b1), .out_3(out_45));
  Pull_Resistor pull_resistor_1 (.node(out_45));
  not not_1 (out_29, A_6);
  Pull_Resistor #(.pull(1)) pull_resistor_2 (.node(out_44));
  trnsstr trnsstr_2 (.in_1(A_6), .in_2(1'b0), .out_3(out_44));
  trnsstr trnsstr_3 (.in_1(B_2), .in_2(1'b1), .out_3(out_34));
  trnsstr trnsstr_4 (.in_1(A_2), .in_2(1'b1), .out_3(out_34));
  or or_1 (out_30, A_2, B_2);
  Pull_Resistor pull_resistor_3 (.node(out_34));
  and and_1 (out_31, A_3, B_3);
  Pull_Resistor pull_resistor_4 (.node(pull_resistor_4_node));
  trnsstr trnsstr_5 (.in_1(A_3), .in_2(1'b1), .out_3(pull_resistor_4_node));
  trnsstr trnsstr_6 (.in_1(B_3), .in_2(pull_resistor_4_node), .out_3(out_35));
  Pull_Resistor pull_resistor_5 (.node(out_35));
  trnsstr trnsstr_7 (.in_1(A), .in_2(1'b1), .out_3(trnsstr_7_out_3));
  trnsstr trnsstr_8 (.in_1(B), .in_2(1'b1), .out_3(trnsstr_7_out_3));
  nor nor_1 (out_27, A, B);
  or or_2 (or_2_out, A, B);
  not not_2 (out_33, or_2_out);
  Pull_Resistor pull_resistor_6 (.node(trnsstr_7_out_3));
  Pull_Resistor #(.pull(1)) pull_resistor_7 (.node(out_39));
  trnsstr trnsstr_9 (.in_1(trnsstr_7_out_3), .in_2(1'b0), .out_3(out_39));
  Pull_Resistor pull_resistor_8 (.node(pull_resistor_8_node));
  trnsstr trnsstr_10 (.in_1(A_4), .in_2(1'b1), .out_3(pull_resistor_8_node));
  nand nand_1 (out_32, A_4, B_4);
  and and_2 (and_2_out, A_4, B_4);
  Pull_Resistor pull_resistor_9 (.node(pull_resistor_9_node));
  trnsstr trnsstr_11 (.in_1(B_4), .in_2(pull_resistor_8_node), .out_3(pull_resistor_9_node));
  not not_3 (out_36, and_2_out);
  Pull_Resistor #(.pull(1)) pull_resistor_10 (.node(out_41));
  trnsstr trnsstr_12 (.in_1(pull_resistor_9_node), .in_2(1'b0), .out_3(out_41));
  Pull_Resistor pull_resistor_11 (.node(pull_resistor_11_node));
  trnsstr trnsstr_13 (.in_1(A_7), .in_2(1'b1), .out_3(pull_resistor_11_node));
  trnsstr trnsstr_14 (.in_1(B_5), .in_2(pull_resistor_11_node), .out_3(trnsstr_14_out_3));
  trnsstr trnsstr_15 (.in_1(A_7), .in_2(1'b1), .out_3(trnsstr_15_out_3));
  trnsstr trnsstr_16 (.in_1(B_5), .in_2(1'b1), .out_3(trnsstr_15_out_3));
  nand nand_2 (nand_2_out, in_19, in_21);
  xor xor_1 (out_37, A_7, B_5);
  Pull_Resistor pull_resistor_12 (.node(trnsstr_14_out_3));
  Pull_Resistor pull_resistor_13 (.node(trnsstr_15_out_3));
  nand nand_3 (nand_3_out, in_15, in_17);
  or or_3 (or_3_out, in_15, in_17);
  nand nand_4 (nand_4_out, in_19, nand_2_out);
  nand nand_5 (nand_5_out, nand_2_out, in_21);
  nor nor_2 (nor_2_out, in_23, in_23);
  nor nor_3 (nor_3_out, in_25, in_25);
  nor nor_4 (nor_4_out, in_25, in_23);
  Pull_Resistor #(.pull(1)) pull_resistor_14 (.node(pull_resistor_14_node));
  trnsstr trnsstr_17 (.in_1(trnsstr_14_out_3), .in_2(1'b0), .out_3(pull_resistor_14_node));
  and and_3 (out_46, nand_3_out, or_3_out);
  nand nand_6 (out_48, nand_4_out, nand_5_out);
  nor nor_5 (nor_5_out, nor_2_out, nor_3_out);
  Pull_Resistor pull_resistor_15 (.node(pull_resistor_15_node));
  trnsstr trnsstr_18 (.in_1(trnsstr_15_out_3), .in_2(1'b1), .out_3(pull_resistor_15_node));
  nor nor_6 (out_51, nor_5_out, nor_4_out);
  Pull_Resistor pull_resistor_16 (.node(out_42));
  trnsstr trnsstr_19 (.in_1(pull_resistor_14_node), .in_2(pull_resistor_15_node), .out_3(out_42));
  Pull_Resistor pull_resistor_17 (.node(pull_resistor_17_node));
  Pull_Resistor pull_resistor_18 (.node(pull_resistor_18_node));
  trnsstr trnsstr_20 (.in_1(A_8), .in_2(1'b1), .out_3(pull_resistor_17_node));
  trnsstr trnsstr_21 (.in_1(B_6), .in_2(pull_resistor_17_node), .out_3(pull_resistor_18_node));
  trnsstr trnsstr_22 (.in_1(A_8), .in_2(1'b1), .out_3(trnsstr_22_out_3));
  trnsstr trnsstr_23 (.in_1(B_6), .in_2(1'b1), .out_3(trnsstr_22_out_3));
  Pull_Resistor pull_resistor_19 (.node(trnsstr_22_out_3));
  nand nand_7 (nand_7_out, in_20, in_22);
  and and_4 (and_4_out, in_16, in_18);
  nor nor_7 (nor_7_out, in_16, in_18);
  nand nand_8 (nand_8_out, in_20, nand_7_out);
  nand nand_9 (nand_9_out, nand_7_out, in_22);
  nor nor_8 (nor_8_out, in_24, in_26);
  xnor xnor_1 (out_38, A_8, B_6);
  Pull_Resistor #(.pull(1)) pull_resistor_20 (.node(pull_resistor_20_node));
  trnsstr trnsstr_24 (.in_1(trnsstr_22_out_3), .in_2(1'b0), .out_3(pull_resistor_20_node));
  or or_4 (out_47, and_4_out, nor_7_out);
  nand nand_10 (nand_10_out, nand_8_out, nand_9_out);
  nor nor_9 (nor_9_out, in_24, nor_8_out);
  nor nor_10 (nor_10_out, nor_8_out, in_26);
  trnsstr trnsstr_25 (.in_1(pull_resistor_20_node), .in_2(1'b1), .out_3(out_43));
  nand nand_11 (out_49, nand_10_out, nand_10_out);
  nor nor_11 (out_50, nor_9_out, nor_10_out);
  trnsstr trnsstr_26 (.in_1(pull_resistor_18_node), .in_2(1'b1), .out_3(out_43));
  Pull_Resistor pull_resistor_21 (.node(out_43));

  assign out_40 = A_5;

  // Notes on the sheet:
  //   Oui / YES
  //   Non / NO
  //   Ou / OR
  //   Et / AND
  //   Non-Ou / NOR
  //   Non-Et / NAND
  //   Toutes
  //   NAND
  //   NOR
  //   Ou-Exclusif / XOR
  //   Non-Ou-Exclusif / XNOR
  //   Toutes
  //   NAND
  //   NOR
endmodule

module trnsstr (
  input  in_1,
  input  in_2,
  output out_3
);

  assign out_3 = in_1 ? in_2 : 1'bz;  // Controlled_Buffer controlled_buffer_1
endmodule
